# Fritzing sketch UPM115 (saved by Fritzing 0.8.7b)
breadboards: 1

parts:
  Part1 = Arduino Nano (Rev3.0)
  S1 = Pushbutton [package="[THT]"]
  OLED2 = WaveShare 1.3 inch OLED
  R1 = Resistor [tolerance=±5% resistance=10k package=THT]

nets:
  GND: Part1.GND, OLED2.GND, R1.Pin_0
  N1: Part1.D2, OLED2.CS
  N2: Part1.D3, OLED2.D/C
  N3: Part1.D4, Part1.D5, OLED2.RES
  N4: Part1.D11/MOSI, OLED2.DIN
  5V: Part1.5V, S1.Pin_3, S1.Pin_4, OLED2.VCC
  N5: Part1.D13/SCK, OLED2.CLK
  N6: S1.Pin_1, S1.Pin_2, R1.Pin_1

custom parts:
  WaveShare 1.3 inch OLED: 128x64 Monochrom OLED Display with a SH1106 controller
